# Fritzing sketch audio_recorder (saved by Fritzing 0.9.3b)
circuit board: 8.46667cm x 5.64444cm
breadboards: 1

parts:
  Part1 = Arduino Nano (Rev3.0) (ICSP)
  LED1 = LED - 5mm [color="Red (633nm)" package="5 mm [THT]"]
  R1 = Resistor [tolerance=±5% resistance=220 package="2010 [SMD]"]
  Part2 = MicroSD Card Module
  Part3 = Breakout Board for Electret Microphone
  S1 = Pushbutton [package="[SMD]"]
  S2 = Pushbutton [package="[SMD]"]
  R2 = Resistor [tolerance=±5% resistance=220 package="2010 [SMD]"]
  R3 = Resistor [tolerance=±5% resistance=220 package="2010 [SMD]"]
  U1 = LIPO-2000mAh [package=lipo-2000]
  R4 = Resistor [tolerance=±5% resistance=220 package="2010 [SMD]"]
  Q1 = NPN-Transistor [package="TO92 [THT]"]
  SP1 = SPEAKER [package=pcb_mount_speaker]

nets:
  GND: Part1.GND, LED1.cathode, Part2.GND, Part3.GND, R2.Pin_0, R3.Pin_0, U1.-, Q1.E
  N1: Part1.D2, S2.Pin_1, S2.Pin_2, R2.Pin_1
  N2: Part1.D3, S1.Pin_1, S1.Pin_2, R3.Pin_1
  N3: Part1.D4, R1.Pin_0
  N4: Part1.D9, R4.Pin_1
  N5: Part1.D10, Part2.CS
  N6: Part1.D11/MOSI, Part2.MOSI
  N7: Part1.D12/MISO, Part2.MISO
  5V: Part1.5V, Part2.VCC, S1.Pin_3, S1.Pin_4, S2.Pin_3, S2.Pin_4, U1.+, SP1.-
  N8: Part1.A0, Part3.AUD
  3V3: Part1.3V3, Part3.VCC
  N9: Part1.D13/SCK, Part2.SCK
  N10: LED1.anode, R1.Pin_1
  N11: R4.Pin_0, Q1.B
  N12: Q1.C, SP1.+
